# Fritzing sketch tcc-esquema (saved by Fritzing 0.9.9b)
breadboards: 1

parts:
  U1 = ESP32S-HiLetgo [part_number=ESP32S-HiLetgo]
  Quarto = LED - 5mm [color="White (4500K)" package="5 mm [THT]"]
  Varanda = LED - 5mm [color="White (4500K)" package="5 mm [THT]"]
  Sótão = LED - 5mm [color="White (4500K)" package="5 mm [THT]"]
  Sala = LED - 5mm [color="White (4500K)" package="5 mm [THT]"]
  Cozinha = LED - 5mm [color="White (4500K)" package="5 mm [THT]"]
  Garagem = LED - 5mm [color="White (4500K)" package="5 mm [THT]"]
  M1 = Humidity and Temperature Sensor DHT11
  U3 = GAS_SENSOR [package=mq-3]
  HC-SR501 = HC-SR501 Body Sensor Module
  J1 = Basic Servo

nets:
  N1: U1.GPIO32, Cozinha.anode
  N2: U1.GPIO33, Sala.anode
  N3: U1.GPIO25, Sótão.anode
  N4: U1.GPIO26, Varanda.anode
  N5: U1.GPIO27, M1.Data
  N6: U1.GPIO14, U3.B1
  N7: U1.GPIO12, HC-SR501.OUT
  GND: U1.GND, Quarto.cathode, Varanda.cathode, Sótão.cathode, Sala.cathode, Cozinha.cathode, Garagem.cathode, M1.GND, U3.A1, HC-SR501.GND, J1.gnd
  N8: U1.GPIO13, Quarto.anode
  VCC: U1.VIN, M1.Vcc, HC-SR501.VCC
  N9: U1.GPIO15, Garagem.anode
  N10: U1.GPIO18, J1.pulse

custom parts:
  ESP32S-HiLetgo: HiLetgo ESP-WROOM-32 ESP32 ESP-32S Development Board 2.4GHz Dual-Mode WiFi + Bluetooth Dual Cores Microcontroller The ESP32 integrated with Antenna switches, RF Balun, power amplifiers, low-noise amplifiers, filters, and management modules, and the entire solution occupies the least area of PCB. 2.4 GHz Wi-Fi plus Bluetooth dual-mode chip, with TSMC Ultra-low power consumption 40nm technology,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
  Humidity and Temperature Sensor DHT11: Digital relative humidity & temperature sensor DHT11
  HC-SR501 Body Sensor Module: Pyroelectric Infrared PIR Motion Sensor Detector Module
